# Fritzing sketch motor (saved by Fritzing 0.9.2b)
breadboards: 1

parts:
  VCC1 = Battery
  M1 = DC Motor
  VCC2 = Battery
  M2 = DC Motor

nets:
  N1: VCC1.-, M1.pin_2
  N2: VCC1.+, M1.pin_1
  N3: VCC2.-, M2.pin_1
  N4: VCC2.+, M2.pin_2
