# Fritzing sketch pulsador_LED (saved by Fritzing 0.9.2b)
breadboards: 1

parts:
  R2 = Resistor [tolerance=±5% resistance=1k package=THT]
  Q1 = NPN-Transistor [package="TO92 [THT]"]
  S1 = Pushbutton [package=THT]
  LED1 = LED - 5mm [color="Red (633nm)" package="5 mm [THT]"]
  VCC1 = Battery
  R1 = Resistor [tolerance=±5% resistance=10k package=THT]

nets:
  N1: R2.Pin_0, LED1.anode
  N2: R2.Pin_1, S1.leg1, VCC1.+
  N3: Q1.E, VCC1.-
  N4: Q1.B, R1.Pin_1
  N5: Q1.C, LED1.cathode
  N6: S1.leg0, R1.Pin_0
