# Fritzing sketch motor_potenciometro (saved by Fritzing 0.9.2b)
breadboards: 1

parts:
  VCC1 = Battery
  R3 = Rotary Potentiometer (Small) [maximum_resistance=10kΩ package=THT]
  Q2 = NPN-Transistor [package="TO92 [THT]"]
  M1 = DC Motor

nets:
  N1: VCC1.-, Q2.E
  N2: VCC1.+, R3.leg1, M1.pin_1
  N3: R3.wiper, Q2.B
  N4: Q2.C, M1.pin_2
