# Fritzing sketch potenciometro_led (saved by Fritzing 0.9.2b)
breadboards: 1

parts:
  VCC1 = Battery
  R1 = Rotary Potentiometer (Small) [maximum_resistance=10kΩ package=THT]
  Q1 = NPN-Transistor [package="TO92 [THT]"]
  R2 = Resistor [tolerance=±10% resistance=1k package=THT]
  LED1 = LED - 5mm [color="Red (633nm)" package="5 mm [THT]"]

nets:
  N1: VCC1.-, Q1.E
  N2: VCC1.+, R1.leg1, LED1.anode
  N3: R1.wiper, Q1.B
  N4: Q1.C, R2.Pin_1
  N5: R2.Pin_0, LED1.cathode
