// Logisim project circuito1.circ as structural Verilog: 1 circuit, main circuit main
module main (
  input  onoff,
  input  v1,
  input  v2,
  input  v3,
  input  p1,
  input  p2,
  output A
);

  wire and_1_out, and_2_out, and_3_out, and_4_out, and_5_out, not_1_out, not_2_out, or_1_out, or_2_out,
       or_3_out;

  not not_1 (not_1_out, p1);
  not not_2 (not_2_out, p2);
  and and_1 (and_1_out, onoff, not_1_out);
  and and_2 (and_2_out, onoff, not_2_out);
  or or_1 (or_1_out, and_1_out, and_2_out);
  and and_3 (and_3_out, onoff, v3);
  and and_4 (and_4_out, onoff, v2);
  and and_5 (and_5_out, onoff, v1);
  or or_2 (or_2_out, or_1_out, and_3_out);
  or or_3 (or_3_out, and_4_out, and_5_out);
  or or_4 (A, or_2_out, or_3_out);
endmodule
