// Logisim project display.circ as structural Verilog: 1 circuit, main circuit main
module main (
  input  b3,
  input  b2,
  input  b1,
  input  b0,
  output a,
  output b,
  output c,
  output d,
  output e,
  output f,
  output g,
  output h
);

  wire undriven, undriven_2, undriven_3, undriven_4, undriven_5, undriven_6, undriven_7, undriven_8;

  _7_Segment_Display u_7_segment_display_1 (
    .g(undriven), .f(undriven_3), .a(undriven_5), .b(undriven_7), .e(undriven_2), .d(undriven_4),
    .c(undriven_6), .dp(undriven_8));
endmodule
